# Fritzing sketch ArduinoScheme (saved by Fritzing 0.9.3b)
breadboards: 1

parts:
  Componente1 = Arduino Uno (Rev3)
  Componente2 = Bluetooth HC-05 Macho
  LED1 = RGB LED (com. cathode, rgb) [package="5 mm [THT]"]
  R1 = Resistor [tolerance=±5% resistance=220 package=THT]
  R2 = Resistor [tolerance=±5% resistance=220 package=THT]
  R3 = Resistor [tolerance=±5% resistance=220 package=THT]

nets:
  N1: Componente1.D9_PWM, Componente1.D10_PWM/SS, R1.Pin_0, R3.Pin_0
  N2: Componente1.D11_PWM/MOSI, R2.Pin_0
  GND: Componente1.GND, Componente2.GND, LED1.common_cathode
  N3: Componente1.D2, Componente2.RXD
  N4: Componente1.D3_PWM, Componente2.TXD
  5V: Componente1.5V, Componente2.VCC
  N5: LED1.red_anode, R2.Pin_1
  N6: LED1.green_anode, R3.Pin_1
  N7: LED1.blue_anode, R1.Pin_1
